# Fritzing sketch Tren (saved by Fritzing 0.9.3b)
breadboards: 1

parts:
  Componente1 = Arduino MKR1000
  R1 = Trimmer Potentiometer [maximum_resistance=10kΩ package=THT]
  LCD1 = LCD screen
  IC1 = L293D [package=THT]
  R2 = Resistor [tolerance=±5% resistance=220 package=THT]
  M1 = DC Motor
  BAT1 = BC9VPC [package=bc9vpc]

nets:
  N1: Componente1.D1, LCD1.DB7
  N2: Componente1.D2_PWM, LCD1.DB6
  N3: Componente1.D3_PWM, IC1.Enable_1
  N4: Componente1.D4_PWM, IC1.In_1
  N5: Componente1.D5_PWM, IC1.In_2
  N6: Componente1.D9_SCK, LCD1.DB5
  N7: Componente1.D10_MISO, LCD1.DB4
  N8: Componente1.D11_SDA, LCD1.E
  N9: Componente1.D12_SCL, LCD1.RS
  GND: Componente1.GND, R1.leg1, LCD1.VSS, LCD1.R/W, LCD1.LED-, IC1.0V, BAT1.V-
  5V: Componente1.5V, R1.leg2, LCD1.VDD, R2.Pin_1
  N10: R1.wiper, LCD1.V0
  N11: LCD1.LED+, R2.Pin_0
  N12: IC1.Out_1_(_Controlled_by_Enable_1_), M1.pin_2
  N13: IC1.Out_2_(_Controlled_by_Enable_1_), M1.pin_1
  N14: IC1.+Vmotor, IC1.+V, BAT1.V+

custom parts:
  Arduino MKR1000: MKR1000 is a powerful board that combines the functionality of the Zero and the Wi-Fi Shield. It is the ideal solution for makers wanting to design IoT projects with minimal previous experience in networking
